# Fritzing sketch AC_SP23_AIP_WK3_buttonsketch (saved by Fritzing 0.9.10b)
breadboards: 1

parts:
  M5Stack-ATOM-Matrix1 = atom-matrix [package=M5Stack]
  LED1 = LED - 5mm [color="Red (635nm)" current=30mA package="5 mm [THT]"]
  R1 = Resistor [tolerance=±5% power=0.25 resistance=220 package=THT]
  S2 = Pushbutton [package=THT]

nets:
  N1: M5Stack-ATOM-Matrix1.G32, LED1.anode
  N2: M5Stack-ATOM-Matrix1.5Vb, S2.leg1
  N3: M5Stack-ATOM-Matrix1.GNDb, R1.Pin_0, S2.leg0
  N4: LED1.cathode, R1.Pin_1

custom parts:
  atom-matrix: M5Stack ATOM Matrix
